// Logisim project Lab4.circ as structural Verilog: 8 circuits, main circuit main
module main (
);

  ALU_Control alu_control_1 ();  // open: ALU_Ctrl1, ALU_Ctrl0, ALU_Src, ALU_Ctrl3, ALU_Ctrl2, I13, I12, I6, I5, I30, I4, I14
endmodule

module ALU_Control (
  input  I30,
  input  I14,
  input  I13,
  input  I12,
  input  I6,
  input  I5,
  input  I4,
  output ALU_Ctrl3,
  output ALU_Ctrl2,
  output ALU_Ctrl1,
  output ALU_Ctrl0,
  output ALU_Src
);

  wire and_2_out, not_1_out, not_2_out, not_3_out, not_4_out, not_5_out, not_6_out, not_7_out;

  not not_1 (not_1_out, I13);
  not not_2 (not_2_out, I13);
  not not_3 (not_3_out, I4);
  not not_4 (not_4_out, I12);
  not not_5 (not_5_out, I5);
  not not_6 (not_6_out, I4);
  and and_1 (ALU_Ctrl2, I30, not_1_out, I5);
  or or_1 (ALU_Ctrl1, not_2_out, not_3_out);
  not not_7 (not_7_out, I14);
  and and_2 (and_2_out, I13, not_4_out);
  or or_2 (ALU_Src, not_5_out, not_6_out);
  or or_3 (ALU_Ctrl0, not_7_out, and_2_out);

  assign ALU_Ctrl3 = 1'b0;
endmodule

module L_1_bit_Adder_a8395dc3 (
  input  A,
  input  B,
  input  C_in,
  output S,
  output C_out
);

  wire and_1_out, and_2_out, xor_1_out;

  xor xor_1 (xor_1_out, A, B);
  xor xor_2 (S, xor_1_out, C_in);
  and and_1 (and_1_out, xor_1_out, C_in);
  and and_2 (and_2_out, A, B);
  or or_1 (C_out, and_1_out, and_2_out);
endmodule

module OneBitALU (
  input  [3:0] ALU_Ctrl,
  input  A,
  input  B,
  input  C_in,
  output R,
  output out_6
);

  wire and_1_out, l_1_bit_adder_a8395dc3_1_s, multiplexer_1_out, not_1_out, or_1_out, xor_1_out;

  not not_1 (not_1_out, B);
  Multiplexer #(.enable("false")) multiplexer_1 (.in0(B), .in1(not_1_out), .out(multiplexer_1_out), .sel(ALU_Ctrl[2]));
  and and_1 (and_1_out, A, multiplexer_1_out);
  or or_1 (or_1_out, A, multiplexer_1_out);
  xor xor_1 (xor_1_out, A, multiplexer_1_out);
  L_1_bit_Adder_a8395dc3 l_1_bit_adder_a8395dc3_1 (
    .A(A), .B(multiplexer_1_out), .C_in(C_in), .S(l_1_bit_adder_a8395dc3_1_s), .C_out(out_6));
  Multiplexer #(.enable("false"), .select(2)) multiplexer_2 (
    .in0(and_1_out), .in1(or_1_out), .in2(xor_1_out), .in3(l_1_bit_adder_a8395dc3_1_s), .out(R),
    .sel(ALU_Ctrl[1:0]));
endmodule

module FourBitALU (
  input  C_in,
  input  [3:0] ALU_Ctrl,
  input  [3:0] A,
  input  [3:0] B,
  output [3:0] Result,
  output O
);

  wire onebitalu_1_out_6, onebitalu_2_out_6, onebitalu_3_out_6;

  OneBitALU onebitalu_1 (
    .ALU_Ctrl(ALU_Ctrl), .A(A[0]), .B(B[0]), .C_in(C_in), .R(Result[0]), .out_6(onebitalu_1_out_6));
  OneBitALU onebitalu_2 (
    .ALU_Ctrl(ALU_Ctrl), .A(A[1]), .B(B[1]), .C_in(onebitalu_1_out_6), .R(Result[1]),
    .out_6(onebitalu_2_out_6));
  OneBitALU onebitalu_3 (
    .ALU_Ctrl(ALU_Ctrl), .A(A[2]), .B(B[2]), .C_in(onebitalu_2_out_6), .R(Result[2]),
    .out_6(onebitalu_3_out_6));
  OneBitALU onebitalu_4 (.ALU_Ctrl(ALU_Ctrl), .A(A[3]), .B(B[3]), .C_in(onebitalu_3_out_6), .R(Result[3]), .out_6(O));
endmodule

module ThirtyTwoReg_New (
  input  [4:0] RReg1,
  input  [31:0] WData,
  input  Clock_In,
  input  Write,
  input  [4:0] WReg,
  input  [4:0] RReg2,
  output [31:0] RData1,
  output [31:0] RData2
);

  wire demultiplexer_1_out0, demultiplexer_1_out1, demultiplexer_1_out2, demultiplexer_1_out3,
       demultiplexer_1_out4, demultiplexer_1_out5, demultiplexer_1_out6, demultiplexer_1_out7,
       demultiplexer_1_out8, demultiplexer_1_out9, demultiplexer_1_out10, demultiplexer_1_out11,
       demultiplexer_1_out12, demultiplexer_1_out13, demultiplexer_1_out14, demultiplexer_1_out15,
       demultiplexer_1_out16, demultiplexer_1_out17, demultiplexer_1_out18, demultiplexer_1_out19,
       demultiplexer_1_out20, demultiplexer_1_out21, demultiplexer_1_out22, demultiplexer_1_out23,
       demultiplexer_1_out24, demultiplexer_1_out25, demultiplexer_1_out26, demultiplexer_1_out27,
       demultiplexer_1_out28, demultiplexer_1_out29, demultiplexer_1_out30, demultiplexer_1_out31;
  wire [31:0] register_1_q, register_2_q, register_3_q, register_4_q, register_5_q, register_6_q,
       register_7_q, register_8_q, register_9_q, register_10_q, register_11_q, register_12_q, register_13_q,
       register_14_q, register_15_q, register_16_q, register_17_q, register_18_q, register_19_q,
       register_20_q, register_21_q, register_22_q, register_23_q, register_24_q, register_25_q,
       register_26_q, register_27_q, register_28_q, register_29_q, register_30_q, register_31_q,
       register_32_q;

  Demultiplexer #(.enable("false"), .select(5)) demultiplexer_1 (
    .out0(demultiplexer_1_out0), .out1(demultiplexer_1_out1), .out2(demultiplexer_1_out2),
    .out3(demultiplexer_1_out3), .out4(demultiplexer_1_out4), .out5(demultiplexer_1_out5),
    .out6(demultiplexer_1_out6), .out7(demultiplexer_1_out7), .out8(demultiplexer_1_out8),
    .out9(demultiplexer_1_out9), .out10(demultiplexer_1_out10), .out11(demultiplexer_1_out11),
    .out12(demultiplexer_1_out12), .out13(demultiplexer_1_out13), .out14(demultiplexer_1_out14),
    .out15(demultiplexer_1_out15), .out16(demultiplexer_1_out16), .out17(demultiplexer_1_out17),
    .out18(demultiplexer_1_out18), .out19(demultiplexer_1_out19), .out20(demultiplexer_1_out20),
    .out21(demultiplexer_1_out21), .out22(demultiplexer_1_out22), .out23(demultiplexer_1_out23),
    .out24(demultiplexer_1_out24), .out25(demultiplexer_1_out25), .out26(demultiplexer_1_out26),
    .out27(demultiplexer_1_out27), .out28(demultiplexer_1_out28), .out29(demultiplexer_1_out29),
    .out30(demultiplexer_1_out30), .out31(demultiplexer_1_out31), .in(Write), .sel(WReg));
  Register #(.width(32)) register_1 (
    .D(WData), .en(demultiplexer_1_out0), .clk(Clock_In), .Q(register_1_q), .clr(Write));
  Register #(.width(32)) register_2 (
    .D(WData), .en(demultiplexer_1_out1), .clk(Clock_In), .Q(register_2_q));  // open: clr
  Register #(.width(32)) register_3 (
    .D(WData), .en(demultiplexer_1_out2), .clk(Clock_In), .Q(register_3_q));  // open: clr
  Register #(.width(32)) register_4 (
    .D(WData), .en(demultiplexer_1_out3), .clk(Clock_In), .Q(register_4_q));  // open: clr
  Register #(.width(32)) register_5 (
    .D(WData), .en(demultiplexer_1_out4), .clk(Clock_In), .Q(register_5_q));  // open: clr
  Register #(.width(32)) register_6 (
    .D(WData), .en(demultiplexer_1_out5), .clk(Clock_In), .Q(register_6_q));  // open: clr
  Register #(.width(32)) register_7 (
    .D(WData), .en(demultiplexer_1_out6), .clk(Clock_In), .Q(register_7_q));  // open: clr
  Register #(.width(32)) register_8 (
    .D(WData), .en(demultiplexer_1_out7), .clk(Clock_In), .Q(register_8_q));  // open: clr
  Register #(.width(32)) register_9 (
    .D(WData), .en(demultiplexer_1_out8), .clk(Clock_In), .Q(register_9_q));  // open: clr
  Register #(.width(32)) register_10 (
    .D(WData), .en(demultiplexer_1_out9), .clk(Clock_In), .Q(register_10_q));  // open: clr
  Register #(.width(32)) register_11 (
    .D(WData), .en(demultiplexer_1_out10), .clk(Clock_In), .Q(register_11_q));  // open: clr
  Register #(.width(32)) register_12 (
    .D(WData), .en(demultiplexer_1_out11), .clk(Clock_In), .Q(register_12_q));  // open: clr
  Register #(.width(32)) register_13 (
    .D(WData), .en(demultiplexer_1_out12), .clk(Clock_In), .Q(register_13_q));  // open: clr
  Register #(.width(32)) register_14 (
    .D(WData), .en(demultiplexer_1_out13), .clk(Clock_In), .Q(register_14_q));  // open: clr
  Register #(.width(32)) register_15 (
    .D(WData), .en(demultiplexer_1_out14), .clk(Clock_In), .Q(register_15_q));  // open: clr
  Register #(.width(32)) register_16 (
    .D(WData), .en(demultiplexer_1_out15), .clk(Clock_In), .Q(register_16_q));  // open: clr
  Register #(.width(32)) register_17 (
    .D(WData), .en(demultiplexer_1_out16), .clk(Clock_In), .Q(register_17_q));  // open: clr
  Register #(.width(32)) register_18 (
    .D(WData), .en(demultiplexer_1_out17), .clk(Clock_In), .Q(register_18_q));  // open: clr
  Register #(.width(32)) register_19 (
    .D(WData), .en(demultiplexer_1_out18), .clk(Clock_In), .Q(register_19_q));  // open: clr
  Register #(.width(32)) register_20 (
    .D(WData), .en(demultiplexer_1_out19), .clk(Clock_In), .Q(register_20_q));  // open: clr
  Register #(.width(32)) register_21 (
    .D(WData), .en(demultiplexer_1_out20), .clk(Clock_In), .Q(register_21_q));  // open: clr
  Register #(.width(32)) register_22 (
    .D(WData), .en(demultiplexer_1_out21), .clk(Clock_In), .Q(register_22_q));  // open: clr
  Register #(.width(32)) register_23 (
    .D(WData), .en(demultiplexer_1_out22), .clk(Clock_In), .Q(register_23_q));  // open: clr
  Register #(.width(32)) register_24 (
    .D(WData), .en(demultiplexer_1_out23), .clk(Clock_In), .Q(register_24_q));  // open: clr
  Register #(.width(32)) register_25 (
    .D(WData), .en(demultiplexer_1_out24), .clk(Clock_In), .Q(register_25_q));  // open: clr
  Register #(.width(32)) register_26 (
    .D(WData), .en(demultiplexer_1_out25), .clk(Clock_In), .Q(register_26_q));  // open: clr
  Register #(.width(32)) register_27 (
    .D(WData), .en(demultiplexer_1_out26), .clk(Clock_In), .Q(register_27_q));  // open: clr
  Register #(.width(32)) register_28 (
    .D(WData), .en(demultiplexer_1_out27), .clk(Clock_In), .Q(register_28_q));  // open: clr
  Register #(.width(32)) register_29 (
    .D(WData), .en(demultiplexer_1_out28), .clk(Clock_In), .Q(register_29_q));  // open: clr
  Register #(.width(32)) register_30 (
    .D(WData), .en(demultiplexer_1_out29), .clk(Clock_In), .Q(register_30_q));  // open: clr
  Register #(.width(32)) register_31 (
    .D(WData), .en(demultiplexer_1_out30), .clk(Clock_In), .Q(register_31_q));  // open: clr
  Register #(.width(32)) register_32 (
    .D(WData), .en(demultiplexer_1_out31), .clk(Clock_In), .Q(register_32_q));  // open: clr
  Multiplexer #(.enable("false"), .select(5), .width(32)) multiplexer_1 (
    .in0(register_1_q), .in1(register_2_q), .in2(register_3_q), .in3(register_4_q), .in4(register_5_q),
    .in5(register_6_q), .in6(register_7_q), .in7(register_8_q), .in8(register_9_q), .in9(register_10_q),
    .in10(register_11_q), .in11(register_12_q), .in12(register_13_q), .in13(register_14_q),
    .in14(register_15_q), .in15(register_16_q), .in16(register_17_q), .in17(register_18_q),
    .in18(register_19_q), .in19(register_20_q), .in20(register_21_q), .in21(register_22_q),
    .in22(register_23_q), .in23(register_24_q), .in24(register_25_q), .in25(register_26_q),
    .in26(register_27_q), .in27(register_28_q), .in28(register_29_q), .in29(register_30_q),
    .in30(register_31_q), .in31(register_32_q), .out(RData1), .sel(RReg1));
  Multiplexer #(.enable("false"), .select(5), .width(32)) multiplexer_2 (
    .in0(register_1_q), .in1(register_2_q), .in2(register_3_q), .in3(register_4_q), .in4(register_5_q),
    .in5(register_6_q), .in6(register_7_q), .in7(register_8_q), .in8(register_9_q), .in9(register_10_q),
    .in10(register_11_q), .in11(register_12_q), .in12(register_13_q), .in13(register_14_q),
    .in14(register_15_q), .in15(register_16_q), .in16(register_17_q), .in17(register_18_q),
    .in18(register_19_q), .in19(register_20_q), .in20(register_21_q), .in21(register_22_q),
    .in22(register_23_q), .in23(register_24_q), .in24(register_25_q), .in25(register_26_q),
    .in26(register_27_q), .in27(register_28_q), .in28(register_29_q), .in29(register_30_q),
    .in30(register_31_q), .in31(register_32_q), .out(RData2), .sel(RReg2));
endmodule

module ALU_32 (
  input  [3:0] ALU_Ctrl,
  input  [31:0] A,
  input  [31:0] B,
  output [31:0] Result,
  output C_out
);

  wire fourbitalu_1_o, fourbitalu_2_o, fourbitalu_3_o, fourbitalu_4_o, fourbitalu_5_o, fourbitalu_6_o,
       fourbitalu_7_o;

  FourBitALU fourbitalu_1 (
    .C_in(ALU_Ctrl[2]), .ALU_Ctrl(ALU_Ctrl), .A(A[3:0]), .B(B[3:0]), .Result(Result[3:0]), .O(fourbitalu_1_o));
  FourBitALU fourbitalu_2 (
    .C_in(fourbitalu_1_o), .ALU_Ctrl(ALU_Ctrl), .A(A[7:4]), .B(B[7:4]), .Result(Result[7:4]),
    .O(fourbitalu_2_o));
  FourBitALU fourbitalu_3 (
    .C_in(fourbitalu_2_o), .ALU_Ctrl(ALU_Ctrl), .A(A[11:8]), .B(B[11:8]), .Result(Result[11:8]),
    .O(fourbitalu_3_o));
  FourBitALU fourbitalu_4 (
    .C_in(fourbitalu_3_o), .ALU_Ctrl(ALU_Ctrl), .A(A[15:12]), .B(B[15:12]), .Result(Result[15:12]),
    .O(fourbitalu_4_o));
  FourBitALU fourbitalu_5 (
    .C_in(fourbitalu_4_o), .ALU_Ctrl(ALU_Ctrl), .A(A[19:16]), .B(B[19:16]), .Result(Result[19:16]),
    .O(fourbitalu_5_o));
  FourBitALU fourbitalu_6 (
    .C_in(fourbitalu_5_o), .ALU_Ctrl(ALU_Ctrl), .A(A[23:20]), .B(B[23:20]), .Result(Result[23:20]),
    .O(fourbitalu_6_o));
  FourBitALU fourbitalu_7 (
    .C_in(fourbitalu_6_o), .ALU_Ctrl(ALU_Ctrl), .A(A[27:24]), .B(B[27:24]), .Result(Result[27:24]),
    .O(fourbitalu_7_o));
  FourBitALU fourbitalu_8 (
    .C_in(fourbitalu_7_o), .ALU_Ctrl(ALU_Ctrl), .A(A[31:28]), .B(B[31:28]), .Result(Result[31:28]), .O(C_out));
endmodule

module Data_Path (
  input  [31:0] Instruction
);

  wire alu_control_1_alu_src, clock_1_out;
  wire [3:0] alu_control_1_alu_ctrl0;
  wire [31:0] alu_32_1_result, bit_extender_1_out, multiplexer_1_out, thirtytworeg_new_1_rdata1,
       thirtytworeg_new_1_rdata2;

  Clock clock_1 (.out(clock_1_out));
  assign bit_extender_1_out = {{20{Instruction[31]}}, Instruction[31:20]};  // Bit_Extender bit_extender_1
  ALU_Control alu_control_1 (
    .ALU_Ctrl1(alu_control_1_alu_ctrl0[1]), .ALU_Ctrl0(alu_control_1_alu_ctrl0[0]),
    .ALU_Src(alu_control_1_alu_src), .ALU_Ctrl3(alu_control_1_alu_ctrl0[3]),
    .ALU_Ctrl2(alu_control_1_alu_ctrl0[2]), .I13(Instruction[13]), .I12(Instruction[12]),
    .I6(Instruction[6]), .I5(Instruction[5]), .I30(Instruction[30]), .I4(Instruction[4]),
    .I14(Instruction[14]));
  ThirtyTwoReg_New thirtytworeg_new_1 (
    .RReg1(Instruction[19:15]), .WData(alu_32_1_result), .Clock_In(clock_1_out), .Write(1'b1),
    .WReg(Instruction[11:7]), .RReg2(Instruction[24:20]), .RData1(thirtytworeg_new_1_rdata1),
    .RData2(thirtytworeg_new_1_rdata2));
  Multiplexer #(.enable("false"), .width(32)) multiplexer_1 (
    .in0(thirtytworeg_new_1_rdata2), .in1(bit_extender_1_out), .out(multiplexer_1_out),
    .sel(alu_control_1_alu_src));
  ALU_32 alu_32_1 (
    .ALU_Ctrl(alu_control_1_alu_ctrl0), .A(thirtytworeg_new_1_rdata1), .B(multiplexer_1_out),
    .Result(alu_32_1_result));  // open: C_out
endmodule
